# Fritzing sketch esquema_emisor (saved by Fritzing 0.9.2b)
breadboards: 1

parts:
  Parte1 = Arduino Uno (Rev3)
  Parte2 = Arduino Xbee Libellium Shield
  U1 = XBEE-1 [package=xbee-silk]
  Parte3 = SRF05 Ultrasonic Rangefinder
  Parte4 = SRF05 Ultrasonic Rangefinder
  Parte5 = SRF05 Ultrasonic Rangefinder

nets:
  N1: Parte1.D9_PWM, Parte4.Echo
  N2: Parte1.D10_PWM/SS, Parte4.Trig
  N3: Parte1.D11_PWM/MOSI, Parte3.Echo
  N4: Parte1.D12/MISO, Parte3.Trig
  N5: Parte1.D6_PWM, Parte5.Echo
  N6: Parte1.D7, Parte5.Trig
  VCC: Parte1.5V, Parte3.VCC, Parte4.VCC, Parte5.VCC
  GND: Parte1.GND, Parte3.GND, Parte4.GND, Parte5.GND
  N7: Parte2.I/08, U1.DIO0
  N8: Parte2.I/02, U1.DIO1
  N9: Parte2.I/03, U1.DIO2
  N10: Parte2.I/06, U1.DIO3
  N11: Parte2.I/05, U1.RTS
  N12: Parte2.15, U1.DIO5
  N13: Parte2.14, Parte2.8, U1.RES
  N14: Parte2.13, U1.DIO9
  N15: Parte2.I/07, U1.CTS
  N16: Parte2.I/04, U1.DIO4
  GND_2: Parte2.GND, U1.GND
  N17: Parte2.9, U1.DTR
  N18: Parte2.PWM1, U1.DIO11
  N19: Parte2.PWM0, U1.RSSI
  N20: Parte2.RST, U1.RESET
  N21: Parte2.4, U1.DIO12
  N22: Parte2.DIN, U1.DIN
  N23: Parte2.DOUT, U1.DOUT
  +3V3: Parte2.+3V3, U1.VDD
