# Fritzing sketch esquema_receptor (saved by Fritzing 0.9.2b)
breadboards: 1

parts:
  Parte2 = LED Matrix - Serial Interface - Red/Green/Blue
  Parte4 = Arduino Xbee Libellium Shield
  U1 = XBEE-1 [package=xbee-1]
  Parte5 = Arduino Uno (Rev3)
  R1 = PHOTOCELL [package=photocell-kit]
  R2 = Resistor [tolerance=±5% resistance=220 package=THT]
  Parte3 = DeuLigne 1.1 - The Snootlab's LCD shield for Arduino

nets:
  VCC: Parte2.VCC, Parte5.5V, R1.P$2
  N1: Parte2.SCK, Parte3.D5
  N2: Parte2.CS, Parte3.D6
  N3: Parte2.MISO, Parte3.D7
  GND: Parte2.GND, Parte5.GND, R2.Pin_1
  N4: Parte4.I/08, U1.DIO0
  N5: Parte4.I/02, U1.DIO1
  N6: Parte4.I/03, U1.DIO2
  N7: Parte4.I/06, U1.DIO3
  N8: Parte4.I/05, U1.RTS
  N9: Parte4.15, U1.DIO5
  N10: Parte4.14, Parte4.8, U1.RES
  N11: Parte4.13, U1.DIO9
  N12: Parte4.I/07, U1.CTS
  N13: Parte4.I/04, U1.DIO4
  GND_2: Parte4.GND, U1.GND
  N14: Parte4.9, U1.DTR
  N15: Parte4.PWM1, U1.DIO11
  N16: Parte4.PWM0, U1.RSSI
  N17: Parte4.RST, U1.RESET
  N18: Parte4.4, U1.DIO12
  N19: Parte4.DIN, U1.DIN
  N20: Parte4.DOUT, U1.DOUT
  +3V3: Parte4.+3V3, U1.VDD
  N21: R1.P$1, R2.Pin_0, Parte3.A5(CLK)
