# Fritzing sketch esquema_receptor_cables (saved by Fritzing 0.9.2b)
breadboards: 1

parts:
  Parte2 = LED Matrix - Serial Interface - Red/Green/Blue
  Parte4 = Arduino Xbee Libellium Shield
  U1 = XBEE-1 [package=xbee-1]
  Parte5 = Arduino Uno (Rev3)
  R1 = PHOTOCELL [package=photocell-kit]
  R2 = Resistor [tolerance=±5% resistance=220 package=THT]
  Parte3 = DeuLigne 1.1 - The Snootlab's LCD shield for Arduino

nets:
  VCC: Parte2.VCC, Parte5.5V, R1.P$2, Parte3.+5V
  N1: Parte2.SCK, Parte4.D5, Parte5.D5_PWM, Parte3.D5
  N2: Parte2.CS, Parte4.D6, Parte5.D6_PWM, Parte3.D6
  N3: Parte2.MISO, Parte4.D7, Parte5.D7, Parte3.D7
  GND: Parte2.GND, Parte5.GND, R2.Pin_1, Parte3.GND
  GND_2: Parte4.GND, U1.GND
  N4: Parte4.M8RXD, Parte5.D0/RX, Parte3.D0_RX
  N5: Parte4.M8TXD, Parte5.D1/TX, Parte3.D1_TX
  N6: Parte4.D2, Parte5.D2, Parte3.D2
  N7: Parte4.D3, Parte5.D3_PWM, Parte3.D3
  N8: Parte4.D4, Parte5.D4, Parte3.D4
  N9: Parte4.I/08, U1.DIO0
  N10: Parte4.I/02, U1.DIO1
  N11: Parte4.I/03, U1.DIO2
  N12: Parte4.I/06, U1.DIO3
  N13: Parte4.I/05, U1.RTS
  N14: Parte4.15, U1.DIO5
  N15: Parte4.14, Parte4.8, U1.RES
  N16: Parte4.13, U1.DIO9
  N17: Parte4.I/07, U1.CTS
  N18: Parte4.I/04, U1.DIO4
  N19: Parte4.A4, Parte5.A4/SDA, Parte3.A4(SDA)
  N20: Parte4.A0, Parte5.A0, Parte3.A0
  N21: Parte4.A1, Parte5.A1, Parte3.A1
  N22: Parte4.A2, Parte5.A2, Parte3.A2
  N23: Parte4.A3, Parte5.A3, Parte3.A3
  N24: Parte4.A5, Parte5.A5/SCL, R1.P$1, R2.Pin_0, Parte3.A5(CLK)
  N25: Parte4.9, U1.DTR
  N26: Parte4.PWM1, U1.DIO11
  N27: Parte4.PWM0, U1.RSSI
  N28: Parte4.RST, U1.RESET
  N29: Parte4.4#67, U1.DIO12
  N30: Parte4.DIN, U1.DIN
  N31: Parte4.DOUT, U1.DOUT
  +3V3: Parte4.+3V3, U1.VDD
  N32: Parte5.D8, Parte3.D8
  N33: Parte5.D9_PWM, Parte3.D9
  N34: Parte5.D10_PWM/SS, Parte3.D10_SS
  N35: Parte5.D11_PWM/MOSI, Parte3.D11_MOSI
  N36: Parte5.D12/MISO, Parte3.D12_MISO
  N37: Parte5.D13/SCK, Parte3.D13_SCK
  N38: Parte5.AREF, Parte3.AREF
  N39: Parte5.RESET, Parte3.RESET
  3V3: Parte5.3V3, Parte3.+3V3
  VIN: Parte5.VIN, Parte3.VIN
